# Fritzing sketch Wiring (saved by Fritzing 0.9.3b)

parts:
  Bauteil1 = Arduino Uno (Rev3)  # not connected
  Bauteil2 = CAN-Bus Shield
  RE1 = Hexadecimal Rotary Encoder [part_number=APEM-PT65-303 package=THT]
  LED1 = smd LED [color="Red (633nm)" package="1206 [SMD]"]
  R1 = Resistor [tolerance=±5% resistance=470 package=THT]
  LED2 = smd LED [color="Red (633nm)" package="1206 [SMD]"]
  R2 = Resistor [tolerance=±5% resistance=470 package=THT]
  R3 = Resistor [tolerance=±5% resistance=100k package=THT]
  R4 = Resistor [tolerance=±5% resistance=100k package=THT]
  R5 = Resistor [tolerance=±5% resistance=100k package=THT]

nets:
  N1: Bauteil2.5V, Bauteil2.D4, RE1.InputCommon, RE1.InputCommon2, R4.Pin_1
  N2: Bauteil2.D3, RE1.Output4Pin, R5.Pin_1
  N3: Bauteil2.D5, RE1.Output1Pin, R3.Pin_1
  N4: Bauteil2.LED1, R2.Pin_1
  N5: Bauteil2.SD_CS, R1.Pin_1
  N6: Bauteil2.GND, LED1.cathode, LED2.cathode
  N7: R3.Pin_0, R4.Pin_0, R5.Pin_0

notes:
  1/2/4
  C
  CHG
  THR
  LEVEL
  470
  100K
